// Logisim project 16 bit computer.circ as structural Verilog
module CPU (
  input  in_1,
  output [7:0] out_2,
  output [7:0] out_3,
  output [7:0] out_4,
  output [7:0] out_5,
  output [7:0] out_6,
  output [7:0] out_7,
  output [7:0] out_8,
  output [7:0] out_9,
  output [7:0] out_10,
  output [7:0] out_11,
  output [7:0] out_12,
  output [7:0] out_13,
  output [7:0] out_14,
  output [7:0] out_15
);

  wire clock_1_out, n2_cycle_1_trigger, n2_cycle_2_trigger, n2_cycle_3_trigger, n2_cycle_4_trigger,
       n2_cycle_5_trigger, n2_cycle_6_trigger, n2_cycle_7_trigger, n2_cycle_8_trigger, n2_cycle_9_trigger,
       n2_cycle_10_trigger, n2_cycle_11_trigger, n2_cycle_12_trigger, n3_cycle_1__1, or_1_out, or_2_out,
       or_3_out, or_4_out, or_5_out, or_6_out, undriven;
  wire [7:0] ram_1_data, transistor_1_out, transistor_2_out, transistor_3_out, transistor_4_out,
       transistor_5_out, transistor_6_out;
  wire [15:0] counter_1_q;

  Counter #(.width(16), .max('hffff), .trigger("falling")) counter_1 (
    .count(in_1), .Q(counter_1_q), .clk(clock_1_out));  // open: load, D, carry, clr
  Clock clock_1 (.out(clock_1_out));
  RAM #(.addrWidth(16)) ram_1 (.addr(counter_1_q), .data(ram_1_data), .clk(clock_1_out));  // open: sel, ld, clr
  _16_Bit_Register u_16_bit_register_1 (
    .mov_al_value8(ram_1_data[7]), .Data(ram_1_data), .CLK(clock_1_out), .ah(out_2), .al(out_3));  // open: mov_ax_value16, mov_ah_value8
  _3_cycle u_3_cycle_1 (.Active(undriven), .CLK(clock_1_out), ._1(n3_cycle_1__1));  // open: _2, _3
  _2_cycle u_2_cycle_1 (.Active(undriven), .CLK(clock_1_out), .Trigger(n2_cycle_1_trigger));
  _2_cycle u_2_cycle_2 (.Active(n3_cycle_1__1), .CLK(clock_1_out), .Trigger(n2_cycle_2_trigger));
  _2_cycle u_2_cycle_3 (.CLK(clock_1_out), .Trigger(n2_cycle_3_trigger));  // open: Active
  _2_cycle u_2_cycle_4 (.CLK(clock_1_out), .Trigger(n2_cycle_4_trigger));  // open: Active
  _2_cycle u_2_cycle_5 (.CLK(clock_1_out), .Trigger(n2_cycle_5_trigger));  // open: Active
  _2_cycle u_2_cycle_6 (.CLK(clock_1_out), .Trigger(n2_cycle_6_trigger));  // open: Active
  _2_cycle u_2_cycle_7 (.CLK(clock_1_out), .Trigger(n2_cycle_7_trigger));  // open: Active
  _2_cycle u_2_cycle_8 (.CLK(clock_1_out), .Trigger(n2_cycle_8_trigger));  // open: Active
  _2_cycle u_2_cycle_9 (.CLK(clock_1_out), .Trigger(n2_cycle_9_trigger));  // open: Active
  _2_cycle u_2_cycle_10 (.CLK(clock_1_out), .Trigger(n2_cycle_10_trigger));  // open: Active
  _2_cycle u_2_cycle_11 (.CLK(clock_1_out), .Trigger(n2_cycle_11_trigger));  // open: Active
  _2_cycle u_2_cycle_12 (.CLK(clock_1_out), .Trigger(n2_cycle_12_trigger));  // open: Active
  or or_1 (or_1_out, n2_cycle_1_trigger, n2_cycle_2_trigger);
  or or_2 (or_2_out, n2_cycle_3_trigger, n2_cycle_4_trigger);
  or or_3 (or_3_out, n2_cycle_5_trigger, n2_cycle_6_trigger);
  or or_4 (or_4_out, n2_cycle_7_trigger, n2_cycle_8_trigger);
  or or_5 (or_5_out, n2_cycle_9_trigger, n2_cycle_10_trigger);
  or or_6 (or_6_out, n2_cycle_11_trigger, n2_cycle_12_trigger);
  Transistor #(.\type ("n"), .width(8)) transistor_1 (.in(ram_1_data), .out(transistor_1_out), .gate(or_1_out));
  Transistor #(.\type ("n"), .width(8)) transistor_2 (.in(ram_1_data), .out(transistor_2_out), .gate(or_2_out));
  Transistor #(.\type ("n"), .width(8)) transistor_3 (.in(ram_1_data), .out(transistor_3_out), .gate(or_3_out));
  Transistor #(.\type ("n"), .width(8)) transistor_4 (.in(ram_1_data), .out(transistor_4_out), .gate(or_4_out));
  Transistor #(.\type ("n"), .width(8)) transistor_5 (.in(ram_1_data), .out(transistor_5_out), .gate(or_5_out));
  Transistor #(.\type ("n"), .width(8)) transistor_6 (.in(ram_1_data), .out(transistor_6_out), .gate(or_6_out));
  Register_small ax (
    .mov_ah_value8(n2_cycle_1_trigger), .mov_al_value8(n2_cycle_2_trigger), .Data_In(transistor_1_out),
    .CLK(clock_1_out), .ah(out_4), .al(out_5));
  Register_small bx (
    .mov_ah_value8(n2_cycle_3_trigger), .mov_al_value8(n2_cycle_4_trigger), .Data_In(transistor_2_out),
    .CLK(clock_1_out), .ah(out_6), .al(out_7));
  Register_small cx (
    .mov_ah_value8(n2_cycle_5_trigger), .mov_al_value8(n2_cycle_6_trigger), .Data_In(transistor_3_out),
    .CLK(clock_1_out), .ah(out_8), .al(out_9));
  Register_small dx (
    .mov_ah_value8(n2_cycle_7_trigger), .mov_al_value8(n2_cycle_8_trigger), .Data_In(transistor_4_out),
    .CLK(clock_1_out), .ah(out_10), .al(out_11));
  Register_small ex (
    .mov_ah_value8(n2_cycle_9_trigger), .mov_al_value8(n2_cycle_10_trigger), .Data_In(transistor_5_out),
    .CLK(clock_1_out), .ah(out_12), .al(out_13));
  Register_small sp (
    .mov_ah_value8(n2_cycle_11_trigger), .mov_al_value8(n2_cycle_12_trigger), .Data_In(transistor_6_out),
    .CLK(clock_1_out), .ah(out_14), .al(out_15));
endmodule

module Register_small (
  input  mov_ah_value8,
  input  mov_al_value8,
  input  [7:0] Data_In,
  input  CLK,
  output [7:0] ah,
  output [7:0] al
);

  wire [7:0] transistor_1_out, transistor_2_out;

  Transistor #(.\type ("n"), .width(8)) transistor_1 (.in(Data_In), .out(transistor_1_out), .gate(mov_ah_value8));
  Transistor #(.\type ("n"), .width(8)) transistor_2 (.in(Data_In), .out(transistor_2_out), .gate(mov_al_value8));
  Register u_ah (.D(transistor_1_out), .en(mov_ah_value8), .Q(ah), .clk(CLK));  // open: clr
  Register u_al (.D(transistor_2_out), .en(mov_al_value8), .Q(al), .clk(CLK));  // open: clr
endmodule

module _2_cycle (
  input  Active,
  input  CLK,
  output Trigger
);

  wire and_1_out, d_ff_1_qn, or_1_out, t_ff_1_q;

  D_Flip_Flop d_ff_1 (
    .clk(CLK), .D(and_1_out), .Q(Trigger), .Qn(d_ff_1_qn), .en(or_1_out), .reset(t_ff_1_q));  // open: preset
  and and_1 (and_1_out, ~Trigger, Active);  // AND_Gate
  or or_1 (or_1_out, and_1_out, t_ff_1_q);
  T_Flip_Flop t_ff_1 (.clk(CLK), .T(Trigger), .Q(t_ff_1_q), .reset(d_ff_1_qn), .en(CLK));  // open: Qn, preset
endmodule

module _3_cycle (
  input  Active,
  input  CLK,
  output _1,
  output _2,
  output _3
);

  wire and_1_out, and_2_out, and_3_out, or_1_out;

  and and_1 (and_1_out, ~or_1_out, Active);  // AND_Gate
  D_Flip_Flop d_ff_1 (.clk(CLK), .D(and_2_out), .Q(_1));  // open: Qn, preset, en, reset
  and and_2 (and_2_out, ~_1, and_1_out);  // AND_Gate
  T_Flip_Flop t_ff_1 (.clk(CLK), .T(_1), .Q(_2), .reset(and_3_out), .en(CLK));  // open: Qn, preset
  and and_3 (and_3_out, _2, _3);
  or or_1 (or_1_out, _1, _2);
  D_Flip_Flop d_ff_2 (.clk(CLK), .D(_2), .Q(_3));  // open: Qn, preset, en, reset
endmodule

module _16_Bit_Register (
  input  mov_ax_value16,
  input  mov_ah_value8,
  input  mov_al_value8,
  input  [7:0] Data,
  input  CLK,
  output [7:0] ah,
  output [7:0] al
);

  wire n2_cycle_1_trigger, n2_cycle_2_trigger, n3_cycle_1__1, or_1_out, or_2_out, or_3_out;
  wire [7:0] transistor_1_out;

  or or_1 (or_1_out, mov_ax_value16, mov_ah_value8);
  or or_2 (or_2_out, n3_cycle_1__1, mov_al_value8);
  _3_cycle u_3_cycle_1 (.Active(mov_ax_value16), .CLK(CLK), ._1(n3_cycle_1__1));  // open: _2, _3
  _2_cycle u_2_cycle_1 (.Active(or_1_out), .CLK(CLK), .Trigger(n2_cycle_1_trigger));
  _2_cycle u_2_cycle_2 (.Active(or_2_out), .CLK(CLK), .Trigger(n2_cycle_2_trigger));
  or or_3 (or_3_out, n2_cycle_1_trigger, n2_cycle_2_trigger);
  Transistor #(.\type ("n"), .width(8)) transistor_1 (.in(Data), .out(transistor_1_out), .gate(or_3_out));
  Register_small ax (
    .mov_ah_value8(n2_cycle_1_trigger), .mov_al_value8(n2_cycle_2_trigger), .Data_In(transistor_1_out),
    .CLK(CLK), .ah(ah), .al(al));
endmodule
